// Logisim project My-PC.circ as structural Verilog: 4 circuits, main circuit main
module main (
);

  latch_cell latch_cell_1 ();  // open: row, write_enable, data_in_out, column, read_enable
endmodule

module and_or_latch (
  input  set,
  input  reset,
  output \output 
);

  wire not_1_out, or_1_out;

  or or_1 (or_1_out, \output , set);
  not not_1 (not_1_out, reset);
  and and_1 (\output , or_1_out, not_1_out);
  LED led_1 (.in(\output ));
endmodule

module gated_latch (
  input  data_input,
  input  write_enable,
  output data_output
);

  wire and_1_out, and_2_out, not_1_out;

  not not_1 (not_1_out, data_input);
  and and_1 (and_1_out, data_input, write_enable);
  and_or_latch and_or_latch_1 (.set(and_1_out), .reset(and_2_out), .\output (data_output));
  and and_2 (and_2_out, not_1_out, write_enable);
endmodule

module latch_cell (
  input  write_enable,
  input  row,
  input  column,
  input  read_enable,
  output data_in_out
);

  wire and_1_out, and_2_out, and_3_out, gated_latch_1_data_output;

  and and_1 (and_1_out, row, column);
  gated_latch gated_latch_1 (
    .data_input(data_in_out), .write_enable(and_2_out), .data_output(gated_latch_1_data_output));
  and and_2 (and_2_out, write_enable, and_1_out);
  and and_3 (and_3_out, and_1_out, read_enable);
  and and_4 (data_in_out, gated_latch_1_data_output, and_3_out);
endmodule
